# Fritzing sketch circuit (saved by Fritzing 0.8.7b)
breadboards: 1

parts:
  U1 = Arduino Uno (Rev3)
  R1 = Resistor [tolerance=±5% resistance=220 package=THT]
  LED1 = LED - 5mm [color="Red (633nm)" package="5 mm [THT]"]

nets:
  N1: U1.D2, R1.Pin_0
  N2: U1.GND, LED1.cathode
  N3: R1.Pin_1, LED1.anode
